// Logisim project D Flip flop.circ as structural Verilog: 1 circuit, main circuit main
module main (
  input  in_1,
  output out_2,
  output out_3
);

  wire clock_1_out, main_1_out_3, not_1_out;

  Clock clock_1 (.out(clock_1_out));
  D_LATCH_without_clock_main main_1 (.in_1(clock_1_out), .in_2(in_1), .out_3(main_1_out_3));  // open: out_4
  not not_1 (not_1_out, clock_1_out);
  D_LATCH_without_clock_main main_2 (.in_1(not_1_out), .in_2(main_1_out_3), .out_3(out_2), .out_4(out_3));
endmodule
